# Fritzing sketch keep.v4_fill (saved by Fritzing 1.0.2b)
circuit board: 8.73595cm x 6.43364cm
breadboards: 1

parts:
  100Klfo = Rotary Potentiometer (Small) [maximum_resistance=100kΩ knob_status=50% power=0.5W package=THT]
  100Km2 = Rotary Potentiometer (Small) [maximum_resistance=100kΩ knob_status=50% power=0.5W package=THT]
  100Kx2 = Rotary Potentiometer (Small) [maximum_resistance=100kΩ knob_status=50% power=0.5W package=THT]
  4040 = CD4040E [package="DIP16 [THT]"]
  XR2206 = XR2206 [package=dil16]
  100Kosc = Rotary Potentiometer (Small) [maximum_resistance=100kΩ knob_status=50% power=0.5W package=THT]
  1uf = Electrolytic Capacitor [capacitance=1µF voltage=16V package="100 mil [THT, electrolytic]"]
  100Km1 = Rotary Potentiometer (Small) [maximum_resistance=100kΩ knob_status=50% power=0.5W package=THT]
  Jm2 = female pin header, 3 pins [form="♀ (female)"]
  j40 = female pin header, 6 pins [form="♀ (female)"]
  4_7k = Resistor [tolerance=±5% resistance=4.7k power=0.25W package=THT]
  Jx1 = female pin header, 2 pins [form="♀ (female)"]
  Jxs = female pin header, 2 pins [form="♀ (female)"]
  100k = Resistor [tolerance=±5% resistance=100k power=0.25W package=THT]
  Jx2 = female pin header, 2 pins [form="♀ (female)"]
  1uf_2 = Electrolytic Capacitor [capacitance=1µF voltage=16V package="100 mil [THT, electrolytic]"]
  4_7k_2 = Resistor [tolerance=±5% resistance=4.7k power=0.25W package=THT]
  68nf = Ceramic Capacitor [capacitance=68nF voltage=16V package="200 mil [THT, multilayer]"]
  330o = Resistor [tolerance=±5% resistance=330 power=0.25W package=THT]
  LED3 = LED - 3mm [color="White (8000K)" current=0.030A package="3 mm [THT]"]
  jlfo = female pin header, 2 pins [form="♀ (female)"]
  10Kflt = Rotary Potentiometer (Small) [maximum_resistance=10kΩ knob_status=50% power=0.5W package=THT]
  1uf_3 = Electrolytic Capacitor [capacitance=1µF voltage=16V package="100 mil [THT, electrolytic]"]
  220o = Resistor [tolerance=±5% resistance=220 power=0.25W package=THT]
  J1 = female pin header, 5 pins [form="♀ (female)"]
  J2 = female pin header, 5 pins [form="♀ (female)"]
  Josc = female pin header, 3 pins [form="♀ (female)"]
  Jm1 = female pin header, 3 pins [form="♀ (female)"]
  LED2 = LED - 3mm [color="White (8000K)" current=0.030A package="3 mm [THT]"]
  100Kx1 = Rotary Potentiometer (Small) [maximum_resistance=100kΩ knob_status=50% power=0.5W package=THT]
  4_7k_3 = Resistor [tolerance=±1% resistance=4.7k power=0.25W package=THT]
  4_7k_4 = Resistor [tolerance=±1% resistance=4.7k power=0.25W package=THT]
  10uf = Electrolytic Capacitor [capacitance=10μF voltage=16V package="100 mil [THT, electrolytic]"]
  100Kmx = Rotary Potentiometer (Small) [maximum_resistance=100kΩ knob_status=50% power=0.5W package=THT]
  4_7k_5 = Resistor [tolerance=±5% resistance=330 power=0.25W package=THT]
  4_7k_6 = Resistor [tolerance=±5% resistance=4.7k power=0.25W package=THT]
  10shape = Rotary Potentiometer (Small) [maximum_resistance=10kΩ knob_status=50% power=0.5W package=THT]
  4_7k3 = Resistor [tolerance=±5% resistance=4.7k power=0.25W package=THT]
  Jamp = female pin header, 2 pins [form="♀ (female)"]
  LDR = Photocell (LDR) [power=0.25W dark_resistance_@0.01lx=300kΩ light_resistance_@100lx=400Ω luminance=10lx package=THT]
  40106 = IC, DIP package, 14 pins [chip_label=40106]
  Jled = female pin header, 3 pins [form="♀ (female)"]
  TRS1 = Audio Jack (TRS) 3.5mm [package="PG203J [THT]"]
  Power_plug1 = Power plug
  j40_2 = female pin header, 2 pins [form="♀ (female)"]
  22 = Ceramic Capacitor [capacitance=0.22µF voltage=16V package="200 mil [THT, multilayer]"]
  1K = Resistor [tolerance=±5% resistance=1k power=0.25W package=THT]
  j41 = female pin header, 4 pins [form="♀ (female)"]
  100n = Ceramic Capacitor [capacitance="100 nF" voltage=35V package="200 mil [THT, multilayer]"]
  47nf = Ceramic Capacitor [capacitance=47nF voltage=16V package="200 mil [THT, multilayer]"]
  out = female pin header, 2 pins [form="♀ (female)"]

nets:
  N1: 100Klfo.wiper, 10uf.+, 40106.pin11
  N2: 100Klfo.leg2, 4040.Input_signal, 330o.Pin_0, 40106.pin10
  N3: 100Km2.leg1, 4040.Q4, Jm2.pin3, j40.pin6
  N4: 100Km2.wiper, Jm2.pin2
  N5: 100Km2.leg2, 4040.Q5, Jm2.pin1, j40.pin4
  N6: 100Kx2.leg1, Jx2.pin1, Jx2.pin2
  N7: 100Kx2.wiper, 4_7k.Pin_1
  GND: 100Kx2.leg2, 4040.Vss, 4040.Reset, XR2206.GND, 1uf.-, LED3.cathode, 1uf_3.-, 100Kx1.leg2, 4_7k_3.Pin_0, 10uf.-, 4_7k_5.Pin_0, 10shape.wiper, 40106.pin7, TRS1.Sleeve, Power_plug1.GND, 22.1, 100n.0, 47nf.0, out.pin1
  N8: 4040.Q13, j40.pin1
  N9: 4040.Q14, j40.pin2
  N10: 4040.Q6, j40.pin3
  N11: 4040.Q7, 100Km1.leg2, j40.pin5, Jm1.pin1
  N12: 4040.Q1, 100Km1.leg1, Jm1.pin3, LED2.anode, j40_2.pin1, j40_2.pin2
  N13: 4040.Q9, j41.pin4
  N14: 4040.Q8, j41.pin3
  N15: 4040.Q10, j41.pin2
  N16: 4040.Q11, j41.pin1
  VCC: 4040.Vdd, XR2206.VCC, 4_7k_4.Pin_0, 40106.pin14, Power_plug1.VCC
  N17: XR2206.AMSI, 4_7k_6.Pin_0
  N18: XR2206.STO, 1uf_2.-
  N19: XR2206.MO, 4_7k3.Pin_1
  N20: XR2206.TC1, 68nf.0
  N21: XR2206.TC2, 68nf.1
  N22: XR2206.TR1, 4_7k_2.Pin_0
  N23: XR2206.TR2, 4_7k.Pin_0
  N24: XR2206.FSKI, Jxs.pin1, Jxs.pin2
  N25: XR2206.WAVEA1, 220o.Pin_1
  N26: XR2206.WAVEA2, 220o.Pin_0
  N27: XR2206.SYMA1, 10shape.leg2
  N28: XR2206.SYMA2, 10shape.leg1
  N29: 100Kosc.wiper, 1uf.+, 100k.Pin_0, 40106.pin9
  N30: 100Kosc.leg2, LDR.pin_0, 40106.pin8
  N31: 100Km1.wiper, Jm1.pin2
  N32: Jx1.pin1, Jx1.pin2, 100Kx1.leg1
  N33: 100k.Pin_1, Josc.pin1, Josc.pin2, Josc.pin3
  N34: 1uf_2.+, 100Kmx.leg1
  N35: 4_7k_2.Pin_1, 100Kx1.wiper
  N36: 330o.Pin_1, jlfo.pin1, jlfo.pin2
  N37: LED3.anode, Jled.pin1, Jled.pin2, Jled.pin3
  N38: 10Kflt.leg1, 1uf_3.+
  N39: 10Kflt.wiper, LDR.pin_1
  N40: 10Kflt.leg2, 100Kmx.leg2, 47nf.1
  N41: J1.pin1, J1.pin2, J1.pin3, J1.pin4, J1.pin5
  N42: J2.pin1, J2.pin2, J2.pin3, J2.pin4, J2.pin5
  N43: LED2.cathode, 4_7k_5.Pin_1
  N44: 4_7k_3.Pin_1, 4_7k_4.Pin_1, 4_7k3.Pin_0
  N45: 100Kmx.wiper, TRS1.Ring, TRS1.Tip, 100n.1, out.pin2
  N46: 4_7k_6.Pin_1, 22.0, 1K.Pin_1
  N47: Jamp.pin1, Jamp.pin2, 1K.Pin_0

notes:
  keep v.5
  blueprint@poetaster.de 2024

custom parts:
  CD4040E: CD4020B, CD4024B, and CD4040B are ripple-carry binary counters. All counter stages are master-slave flip-flops. The state of a counter advances one count on the negative transition of each input pulse; a high level on the RESET line resets the counter to its all zeros state. Schmitt trigger action on the input-pulse line permits unlimited rise and fall times. All inputs and outputs are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
